// Logisim project carry_lookahead_adder.circ as structural Verilog: 1 circuit, main circuit main
module main (
  input  in_1,
  input  in_2,
  input  in_3,
  input  in_4,
  input  in_5,
  input  in_6,
  input  in_7,
  input  in_8,
  input  in_9
);

  wire and_1_out, and_2_out, and_3_out, and_4_out, and_5_out, and_6_out, and_7_out, and_8_out, and_9_out,
       and_10_out, and_11_out, and_12_out, and_13_out, and_14_out, and_15_out, and_16_out, and_17_out,
       and_18_out, and_19_out, or_1_out, or_2_out, or_3_out, or_4_out, or_5_out, or_6_out, or_7_out,
       or_8_out, or_9_out, or_10_out, or_11_out, or_12_out, xor_1_out, xor_2_out, xor_3_out, xor_4_out,
       xor_5_out, xor_6_out, xor_7_out, xor_8_out;

  // Probe on xor_1_out
  or or_1 (or_1_out, and_1_out, and_2_out);
  xor xor_1 (xor_1_out, xor_2_out, or_3_out);
  and and_1 (and_1_out, xor_2_out, or_3_out);
  and and_2 (and_2_out, in_5, in_1);
  and and_3 (and_3_out, in_5, in_1);
  or or_2 (or_2_out, in_5, in_1);
  xor xor_2 (xor_2_out, in_5, in_1);
  // Probe on xor_3_out
  xor xor_3 (xor_3_out, xor_4_out, or_7_out);
  and and_4 (and_4_out, xor_4_out, or_7_out);
  or or_3 (or_3_out, and_4_out, and_5_out);
  and and_5 (and_5_out, in_6, in_2);
  and and_6 (and_6_out, in_6, in_2);
  or or_4 (or_4_out, in_6, in_2);
  xor xor_4 (xor_4_out, in_6, in_2);
  or or_5 (or_5_out, or_6_out, and_8_out);
  or or_6 (or_6_out, and_3_out, and_12_out);
  and and_7 (and_7_out, and_13_out, and_14_out);
  and and_8 (and_8_out, and_7_out, in_9);
  // Probe on xor_5_out
  xor xor_5 (xor_5_out, xor_6_out, or_11_out);
  and and_9 (and_9_out, xor_6_out, or_11_out);
  or or_7 (or_7_out, and_9_out, and_10_out);
  and and_10 (and_10_out, in_7, in_3);
  and and_11 (and_11_out, in_7, in_3);
  or or_8 (or_8_out, in_7, in_3);
  and and_12 (and_12_out, or_2_out, or_9_out);
  and and_13 (and_13_out, or_2_out, or_4_out);
  and and_14 (and_14_out, or_8_out, or_12_out);
  xor xor_6 (xor_6_out, in_7, in_3);
  or or_9 (or_9_out, and_6_out, and_15_out);
  and and_15 (and_15_out, or_4_out, or_10_out);
  or or_10 (or_10_out, and_11_out, and_16_out);
  // Probe on xor_7_out
  xor xor_7 (xor_7_out, xor_8_out, in_9);
  or or_11 (or_11_out, and_17_out, and_18_out);
  and and_16 (and_16_out, or_8_out, and_19_out);
  xor xor_8 (xor_8_out, in_8, in_4);
  and and_17 (and_17_out, xor_8_out, in_9);
  and and_18 (and_18_out, in_8, in_4);
  and and_19 (and_19_out, in_8, in_4);
  or or_12 (or_12_out, in_8, in_4);

  // Notes on the sheet:
  //   c_out
  //   g
  //   p
  //   c_out
  //   g
  //   p
  //   c_out
  //   g 3:0
  //   c_in * p_3:0
  //   c_out
  //   g
  //   p
  //   g3 + (p3 * c2)
  //   c2
  //   g2 + (p2 * c1)
  //   c1
  //   c_out
  //   g
  //   p
  //   g1 + (p1 * g0)
endmodule
